// Digital circuit clockctrl.dig as structural Verilog
module clockctrl (
  input  clock,
  input  step,
  input  run,
  input  erun,
  output stall
);

  wire and_1_out, d_ff_1_q, d_ff_2_nq, d_ff_as_1_q, or_1_out, or_2_out, or_3_out;

  or or_1 (or_1_out, erun, run);
  D_FF d_ff_1 (.D(step), .C(clock), .Q(d_ff_1_q));  // open: nQ
  D_FF d_ff_2 (.D(d_ff_1_q), .C(clock), .nQ(d_ff_2_nq));  // open: Q
  or or_2 (or_2_out, d_ff_as_1_q, or_1_out);
  and and_1 (and_1_out, d_ff_1_q, d_ff_2_nq);
  D_FF_AS d_ff_as_1 (.Set(1'b0), .D(or_2_out), .C(clock), .Clr(and_1_out), .Q(d_ff_as_1_q));  // open: nQ
  or or_3 (or_3_out, d_ff_as_1_q, and_1_out);
  D_FF d_ff_3 (.D(or_3_out), .C(clock), .nQ(stall));  // open: Q

  // Notes on the sheet:
  //   clock: Hz: 10
endmodule
