// Digital circuit control.dig as structural Verilog
module control (
  input  sys,
  input  [4:0] op,
  input  stall,
  input  clock,
  input  t_in,
  output [2:0] aluop,
  output T,
  output halt,
  output error,
  output mem,
  output [1:0] memop,
  output en_fetch,
  output jump
);

  wire and_2_out, and_3_out, and_4_out, not_2_out, xor_1_out;
  wire [0:0] and_1_out;

  not not_1 (en_fetch, stall);
  and and_1 (and_1_out[0], ~op[3], op[4], ~sys, en_fetch);  // And
  and and_2 (and_2_out, op[1], op[2], ~op[3], ~op[4]);  // And
  and and_3 (and_3_out, op[2], ~op[3], ~op[4]);  // And
  Register u_T (.D(t_in), .C(clock), .en(en_fetch), .Q(T));
  and and_4 (and_4_out, op[0], ~op[1], sys, en_fetch);  // And
  and and_5 (mem, en_fetch, ~sys, ~op[4], ~op[3], ~op[2]);  // And
  Multiplexer #(.Selector_Bits(2), .Bits(3)) multiplexer_1 (
    .sel({mem, and_1_out[0]}), .in_0(3'b111), .in_1(op[2:0]), .in_2(3'b000), .in_3(3'b000), .out(aluop));
  xor xor_1 (xor_1_out, op[0], T);
  not not_2 (not_2_out, T);
  Multiplexer multiplexer_2 (.sel(and_2_out), .in_0(and_3_out), .in_1(xor_1_out), .out(jump));
  and and_6 (halt, T, and_4_out);
  and and_7 (error, and_4_out, not_2_out);
  Multiplexer #(.Bits(2)) multiplexer_3 (.sel(mem), .in_0(2'b00), .in_1(op[1:0]), .out(memop));

  // Other names for the same wires on the sheet: en_halt = en_fetch; en_mem = en_fetch; en_reg = en_fetch;
  //   en_T = en_fetch

  // Notes on the sheet:
  //   Alu Ops
  //   Conditional
  //   Branches
  //   Branches
  //   Mem Access
  //   Stall Logic
  //   Nop Logic
  //   Halt
  //   Take
  //   Branch
  //   Halt Logic
endmodule

/* Test case ALU Ops:
op      sys stall aluop jump halt error mem memop
0b10000 0   0     0     0    0    0     0   0
0b11000 0   0     7     0    0    0     0   0
0b10011 0   0     3     0    0    0     0   0
0b01011 0   0     7     0    0    0     0   0
0b10011 0   1     7     0    0    0     0   0
*/

/* Test case Branches:
op      sys stall clock t_in aluop jump en_fetch halt error mem memop
0b00100 0   0     0     0    7     1    1        0    0     0   0

# with T clear
0b00110 0   0     0     0    7     0    1        0    0     0   0
0b00111 0   0     0     0    7     1    1        0    0     0   0

# with T set
0b00110 0   0     1     1    7     1    1        0    0     0   0
0b00111 0   0     1     1    7     0    1        0    0     0   0

# stalled
0b00100 0   1     0     0    7     1    0        0    0     0   0
0b00110 0   1     0     0    7     1    0        0    0     0   0
0b00111 0   1     0     0    7     0    0        0    0     0   0
0b00110 0   1     1     1    7     1    0        0    0     0   0
0b00111 0   1     1     1    7     0    0        0    0     0   0
*/

/* Test case Halt:
op      sys stall clock t_in aluop jump halt error mem memop

# with T clear
0b00001 1   0     0     0    7     0    0    1     0   0

# with T set
0b00001 1   0     1     1    7     0    1    0     0   0

# reset T
0b00001 1   0     1     0    7     0    1    0     0   0
0b00001 1   0     1     0    7     0    1    0     0   0

# check stall
0b00001 1   1     0     0    7     0    0    0     0   0
0b00001 1   1     1     1    7     0    0    0     0   0
*/

/* Test case Mem Access:
op      sys stall aluop jump halt error mem memop

0b00000 0   0     0     0    0    0     1   0
0b00001 0   0     0     0    0    0     1   1
0b00011 0   0     0     0    0    0     1   3

0b00000 0   1     7     0    0    0     0   0
0b00001 0   1     7     0    0    0     0   0
0b00011 0   1     7     0    0    0     0   0
*/
