// Digital circuit debugreg.dig as structural Verilog
module debugreg (
  input  [25:0] i,
  input  [7:0] s,
  input  [25:0] o,
  output [15:0] v
);

  debugval debugval_1 (.db_i(i), .sel(s), .db_o(o), .Q(v));
endmodule
