// Digital circuit execute.dig as structural Verilog
module execute (
  input  [15:0] L,
  input  [15:0] R,
  input  [2:0] op,
  input  [2:0] cond,
  output [15:0] L_out,
  output [15:0] R_out,
  output [15:0] result,
  output skip_n
);

  wire and_2_out, and_3_out, C, eq, ge, hs, lt, N, ne, RN, V;
  wire [14:0] add_1_s, multiplexer_1_out;
  wire [15:0] and_1_out, funnelshifter_1_o, not_1_out, or_1_out, \xor ;

  Multiplexer #(.Bits(16)) multiplexer_1 (.sel(op[0]), .in_0(R), .in_1(not_1_out), .out({RN, multiplexer_1_out}));
  assign not_1_out = ~R;  // Not not_1, 16 bits wide
  Add #(.Bits(16)) add_1 (.a(L), .b({RN, multiplexer_1_out}), .c_i(op[0]), .s({N, add_1_s}), .c_o(C));
  funnelshifter funnelshifter_1 (.I(L), .amt(R[3:0]), .dir(op[0]), .arith(op[2]), .O(funnelshifter_1_o));
  assign \xor  = L ^ R;  // XOr xor_1, 16 bits wide
  assign and_1_out = L & R;  // And and_1, 16 bits wide
  assign or_1_out = L | R;  // Or or_1, 16 bits wide
  Multiplexer #(.Selector_Bits(3), .Bits(16)) multiplexer_2 (
    .sel(op), .in_0({N, add_1_s}), .in_1({N, add_1_s}), .in_2(funnelshifter_1_o), .in_3(funnelshifter_1_o),
    .in_4(funnelshifter_1_o), .in_5(\xor ), .in_6(and_1_out), .in_7(or_1_out), .out(result));
  xor xor_2 (ge, N, V);
  Comparator #(.Bits(16)) u_eq (.a(\xor ), .b({16{1'b0}}), .eq(ne));  // open: gt, lt
  and and_2 (and_2_out, L[15], RN, ~N);  // And
  and and_3 (and_3_out, ~L[15], ~RN, N);  // And
  not not_2 (lt, ge);
  not not_3 (hs, C);
  not not_4 (eq, ne);
  or or_2 (V, and_2_out, and_3_out);
  Multiplexer #(.Selector_Bits(3)) multiplexer_3 (
    .sel(cond), .in_0(1'b0), .in_1(eq), .in_2(ne), .in_3(lt), .in_4(ge), .in_5(C), .in_6(hs), .in_7(1'b0),
    .out(skip_n));

  assign L_out = L;
  assign R_out = R;

  // Other names for the same wires on the sheet: LN = L[15]; lo = C
endmodule
