// Digital circuit fetch.dig as structural Verilog
module fetch (
  input  [15:0] instr_i,
  input  clock,
  input  en,
  input  jump,
  input  [15:0] value,
  output [15:0] instr_o,
  output [7:0] pc
);

  wire and_1_out;
  wire [15:0] multiplexer_1_out;

  Multiplexer #(.Bits(16)) multiplexer_1 (.sel(jump), .in_0(instr_i), .in_1({16{1'b0}}), .out(multiplexer_1_out));
  and and_1 (and_1_out, en, jump);
  Register #(.Bits(16)) IR (.D(multiplexer_1_out), .C(clock), .en(en), .Q(instr_o));
  CounterPreset #(.Bits(8), .isProgramCounter("true")) u_PC (
    .en(en), .C(clock), .dir(1'b0), .in(value[7:0]), .ld(and_1_out), .clr(1'b0), .out(pc));  // open: ovf
endmodule
