// Digital circuit frontpanel.dig as structural Verilog
module frontpanel (
  input  clock,
  input  erun,
  input  DC,
  output [15:0] R0,
  output [15:0] R1,
  output [15:0] R2,
  output [15:0] R3,
  output [15:0] PC,
  output halt,
  output error,
  output [15:0] R4,
  output [15:0] R5,
  output [15:0] R6,
  output [15:0] R7
);

  wire aluopdisplay_1_p1, aluopdisplay_1_p2, busdisplay_1_p1, busdisplay_1_p2, busdisplay_1_p3,
       busdisplay_1_p4, busdisplay_1_p5, busdisplay_2_p1, busdisplay_2_p2, busdisplay_2_p3, busdisplay_2_p4,
       busdisplay_2_p5, busdisplay_3_p1, busdisplay_3_p2, busdisplay_3_p3, busdisplay_3_p4, busdisplay_3_p5,
       busdisplay_4_p1, busdisplay_4_p2, busdisplay_4_p3, busdisplay_4_p4, busdisplay_4_p5, debugreg_1_p3,
       debugreg_3_p3, debugreg_4_p3, debugreg_5_p3, debugreg_6_p3, debugreg_7_p3, debugreg_8_p3,
       dipswitch_1_out, hex, instrdisplay_1_p1, instrdisplay_1_p2, instrdisplay_1_p3, instrdisplay_1_p4,
       instrdisplay_1_p5, instrdisplay_1_p6, MC, rddisplay_1_p1, rddisplay_1_p2, rddisplay_1_p3,
       rddisplay_2_p1, rddisplay_2_p2, rddisplay_2_p3, rddisplay_3_p1, rddisplay_3_p2, rddisplay_3_p3,
       rj32_1_req, rj32_1_w_en, run_t, skip, slow_t, stalled_t, step_t, undriven_2;
  wire [3:0] busdisplay_1_d1, busdisplay_1_d2, busdisplay_1_d3, busdisplay_1_d4, busdisplay_1_d5,
       busdisplay_2_d1, busdisplay_2_d2, busdisplay_2_d3, busdisplay_2_d4, busdisplay_2_d5, busdisplay_3_d1,
       busdisplay_3_d2, busdisplay_3_d3, busdisplay_3_d4, busdisplay_3_d5, busdisplay_4_d1, busdisplay_4_d2,
       busdisplay_4_d3, busdisplay_4_d4, busdisplay_4_d5;
  wire [7:0] rj32_1_a_prog;
  wire [15:0] aluopdisplay_1_d1, aluopdisplay_1_d2, instrdisplay_1_d1, instrdisplay_1_d2, instrdisplay_1_d3,
       instrdisplay_1_d4, instrdisplay_1_d5, instrdisplay_1_d6, Program_d, rddisplay_1_d1, rddisplay_1_d2,
       rddisplay_1_d3, rddisplay_2_d1, rddisplay_2_d2, rddisplay_2_d3, rddisplay_3_d1, rddisplay_3_d2,
       rddisplay_3_d3, rj32_1_a_data, rj32_1_d_out, undriven;
  wire [25:0] aluopdisplay_1_o, busdisplay_1_o, busdisplay_2_o, db, instrdisplay_1_o, rddisplay_1_o,
       rddisplay_2_o, rddisplay_3_o;

  Button step (.out(step_t));
  Button slow (.out(slow_t));
  Button run (.out(run_t));
  LED stalled (.in(stalled_t));
  BlockRAMDualPort #(.AddrBits(8), .isProgramMemory("true"), .Bits(16)) Program (
    .A(rj32_1_a_prog), .Din({16{1'b0}}), .str(1'b0), .C(MC), .D(Program_d));
  SixteenSeg sixteenseg_1 (.led(rddisplay_1_d1), .dp(rddisplay_1_p1));
  rddisplay rddisplay_1 (
    .D1(rddisplay_1_d1), .P1(rddisplay_1_p1), .D2(rddisplay_1_d2), .P2(rddisplay_1_p2), .D3(rddisplay_1_d3),
    .P3(rddisplay_1_p3), .i(db), .o(rddisplay_1_o), .C(1'b0));
  SixteenSeg sixteenseg_2 (.led(instrdisplay_1_d1), .dp(instrdisplay_1_p1));
  SixteenSeg sixteenseg_3 (.led(instrdisplay_1_d2), .dp(instrdisplay_1_p2));
  instrdisplay instrdisplay_1 (
    .D1(instrdisplay_1_d1), .P1(instrdisplay_1_p1), .D2(instrdisplay_1_d2), .P2(instrdisplay_1_p2),
    .D3(instrdisplay_1_d3), .P3(instrdisplay_1_p3), .D4(instrdisplay_1_d4), .P4(instrdisplay_1_p4),
    .D5(instrdisplay_1_d5), .P5(instrdisplay_1_p5), .D6(instrdisplay_1_d6), .P6(instrdisplay_1_p6), .i(db),
    .o(instrdisplay_1_o));
  SixteenSeg sixteenseg_4 (.led(rddisplay_1_d2), .dp(rddisplay_1_p2));
  SixteenSeg sixteenseg_5 (.led(rddisplay_1_d3), .dp(rddisplay_1_p3));
  rj32 rj32_1 (
    .stall(stalled_t), .skip(skip), .halt(halt), .error(error), .db(db), .erun(erun), .run_faster(1'b1),
    .run_fast(run_t), .run_slow(slow_t), .step(step_t), .clock(clock), .A_prog(rj32_1_a_prog),
    .D_prog(Program_d), .clock_m(MC), .w_en(rj32_1_w_en), .D_out(rj32_1_d_out), .A_data(rj32_1_a_data),
    .D_in(undriven), .req(rj32_1_req), .ack(undriven_2));
  datamemio datamemio_1 (
    .we(rj32_1_w_en), .D_in(rj32_1_d_out), .A(rj32_1_a_data), .D_out(undriven), .req(rj32_1_req),
    .ack(undriven_2), .clk(clock));
  SixteenSeg sixteenseg_6 (.led(instrdisplay_1_d3), .dp(instrdisplay_1_p3));
  SixteenSeg sixteenseg_7 (.led(instrdisplay_1_d4), .dp(instrdisplay_1_p4));
  Seven_Seg_Hex seven_seg_hex_1 (.d(busdisplay_1_d1), .dp(busdisplay_1_p1));
  busdisplay busdisplay_1 (
    .D1(busdisplay_1_d1), .P1(busdisplay_1_p1), .D2(busdisplay_1_d2), .P2(busdisplay_1_p2),
    .D3(busdisplay_1_d3), .P3(busdisplay_1_p3), .D4(busdisplay_1_d4), .P4(busdisplay_1_p4),
    .D5(busdisplay_1_d5), .P5(busdisplay_1_p5), .i(rddisplay_1_o), .o(busdisplay_1_o), .C(2'b11), .H(hex));
  SixteenSeg sixteenseg_8 (.led(instrdisplay_1_d5), .dp(instrdisplay_1_p5));
  SixteenSeg sixteenseg_9 (.led(instrdisplay_1_d6), .dp(instrdisplay_1_p6));
  Seven_Seg_Hex seven_seg_hex_2 (.d(busdisplay_1_d2), .dp(busdisplay_1_p2));
  Seven_Seg_Hex seven_seg_hex_3 (.d(busdisplay_1_d3), .dp(busdisplay_1_p3));
  SixteenSeg sixteenseg_10 (.led(rddisplay_2_d1), .dp(rddisplay_2_p1));
  Seven_Seg_Hex seven_seg_hex_4 (.d(busdisplay_1_d4), .dp(busdisplay_1_p4));
  Seven_Seg_Hex seven_seg_hex_5 (.d(busdisplay_1_d5), .dp(busdisplay_1_p5));
  SixteenSeg sixteenseg_11 (.led(rddisplay_2_d2), .dp(rddisplay_2_p2));
  SixteenSeg sixteenseg_12 (.led(rddisplay_2_d3), .dp(rddisplay_2_p3));
  rddisplay rddisplay_2 (
    .D1(rddisplay_2_d1), .P1(rddisplay_2_p1), .D2(rddisplay_2_d2), .P2(rddisplay_2_p2), .D3(rddisplay_2_d3),
    .P3(rddisplay_2_p3), .i(instrdisplay_1_o), .o(rddisplay_2_o), .C(1'b0));
  Seven_Seg_Hex seven_seg_hex_6 (.d(busdisplay_2_d1), .dp(busdisplay_2_p1));
  busdisplay busdisplay_2 (
    .D1(busdisplay_2_d1), .P1(busdisplay_2_p1), .D2(busdisplay_2_d2), .P2(busdisplay_2_p2),
    .D3(busdisplay_2_d3), .P3(busdisplay_2_p3), .D4(busdisplay_2_d4), .P4(busdisplay_2_p4),
    .D5(busdisplay_2_d5), .P5(busdisplay_2_p5), .i(busdisplay_1_o), .o(busdisplay_2_o), .C(2'b01), .H(hex));
  SixteenSeg sixteenseg_13 (.led(rddisplay_3_d1), .dp(rddisplay_3_p1));
  DipSwitch u_hex (.out(hex));
  Seven_Seg_Hex seven_seg_hex_7 (.d(busdisplay_2_d2), .dp(busdisplay_2_p2));
  Seven_Seg_Hex seven_seg_hex_8 (.d(busdisplay_2_d3), .dp(busdisplay_2_p3));
  SixteenSeg sixteenseg_14 (.led(rddisplay_3_d2), .dp(rddisplay_3_p2));
  SixteenSeg sixteenseg_15 (.led(rddisplay_3_d3), .dp(rddisplay_3_p3));
  rddisplay rddisplay_3 (
    .D1(rddisplay_3_d1), .P1(rddisplay_3_p1), .D2(rddisplay_3_d2), .P2(rddisplay_3_p2), .D3(rddisplay_3_d3),
    .P3(rddisplay_3_p3), .i(rddisplay_2_o), .o(rddisplay_3_o), .C(1'b1));
  Seven_Seg_Hex seven_seg_hex_9 (.d(busdisplay_2_d4), .dp(busdisplay_2_p4));
  Seven_Seg_Hex seven_seg_hex_10 (.d(busdisplay_2_d5), .dp(busdisplay_2_p5));
  DipSwitch dipswitch_1 (.out(dipswitch_1_out));
  Seven_Seg_Hex seven_seg_hex_11 (.d(busdisplay_3_d1), .dp(busdisplay_3_p1));
  SixteenSeg sixteenseg_16 (.led(aluopdisplay_1_d1), .dp(aluopdisplay_1_p1));
  aluopdisplay aluopdisplay_1 (
    .D1(aluopdisplay_1_d1), .P1(aluopdisplay_1_p1), .D2(aluopdisplay_1_d2), .P2(aluopdisplay_1_p2),
    .i(busdisplay_2_o), .o(aluopdisplay_1_o));
  // debugreg debugreg_1: pin names not known; wires that end beside it: 8'h17, db, debugreg_1_p3, PC
  // debugreg debugreg_2: pin names not known; wires that end beside it: {8{1'b0}}, debugreg_1_p3, R0
  vga_frontpanel vga_frontpanel_1 (.clock(DC), .en(dipswitch_1_out), .db(db));
  Seven_Seg_Hex seven_seg_hex_12 (.d(busdisplay_3_d2), .dp(busdisplay_3_p2));
  Seven_Seg_Hex seven_seg_hex_13 (.d(busdisplay_3_d3), .dp(busdisplay_3_p3));
  busdisplay busdisplay_3 (
    .D1(busdisplay_3_d1), .P1(busdisplay_3_p1), .D2(busdisplay_3_d2), .P2(busdisplay_3_p2),
    .D3(busdisplay_3_d3), .P3(busdisplay_3_p3), .D4(busdisplay_3_d4), .P4(busdisplay_3_p4),
    .D5(busdisplay_3_d5), .P5(busdisplay_3_p5), .i(rddisplay_3_o), .C(2'b00), .H(hex));  // open: o
  SixteenSeg sixteenseg_17 (.led(aluopdisplay_1_d2), .dp(aluopdisplay_1_p2));
  Seven_Seg_Hex seven_seg_hex_14 (.d(busdisplay_3_d4), .dp(busdisplay_3_p4));
  Seven_Seg_Hex seven_seg_hex_15 (.d(busdisplay_3_d5), .dp(busdisplay_3_p5));
  Seven_Seg_Hex seven_seg_hex_16 (.d(busdisplay_4_d1), .dp(busdisplay_4_p1));
  Seven_Seg_Hex seven_seg_hex_17 (.d(busdisplay_4_d2), .dp(busdisplay_4_p2));
  busdisplay busdisplay_4 (
    .D1(busdisplay_4_d1), .P1(busdisplay_4_p1), .D2(busdisplay_4_d2), .P2(busdisplay_4_p2),
    .D3(busdisplay_4_d3), .P3(busdisplay_4_p3), .D4(busdisplay_4_d4), .P4(busdisplay_4_p4),
    .D5(busdisplay_4_d5), .P5(busdisplay_4_p5), .i(aluopdisplay_1_o), .C(2'b10), .H(hex));  // open: o
  Seven_Seg_Hex seven_seg_hex_18 (.d(busdisplay_4_d3), .dp(busdisplay_4_p3));
  Seven_Seg_Hex seven_seg_hex_19 (.d(busdisplay_4_d4), .dp(busdisplay_4_p4));
  Seven_Seg_Hex seven_seg_hex_20 (.d(busdisplay_4_d5), .dp(busdisplay_4_p5));
  // debugreg debugreg_3: pin names not known; wires that end beside it: 8'h1, db, debugreg_3_p3, R1
  // debugreg debugreg_4: pin names not known; wires that end beside it: 8'h2, debugreg_3_p3, debugreg_4_p3, R2
  // debugreg debugreg_5: pin names not known; wires that end beside it: 8'h3, debugreg_4_p3, debugreg_5_p3, R3
  // debugreg debugreg_6: pin names not known; wires that end beside it: 8'h4, debugreg_5_p3, debugreg_6_p3, R4
  // debugreg debugreg_7: pin names not known; wires that end beside it: 8'h5, debugreg_6_p3, debugreg_7_p3, R5
  // debugreg debugreg_8: pin names not known; wires that end beside it: 8'h6, debugreg_7_p3, debugreg_8_p3, R6
  // debugreg debugreg_9: pin names not known; wires that end beside it: 8'h7, debugreg_8_p3, R7
  LED u_skip (.in(skip));

  // Other names for the same wires on the sheet: C = clock

  // Notes on the sheet:
  //   clock: Hz: 800
  //   DC: Hz: 2147483647
  //   rj45 Creates
  //   =
endmodule
