// Digital circuit instdecoder.dig as structural Verilog
module instdecoder (
  input  [2:0] fmt,
  input  [1:0] op1,
  input  [3:0] op2,
  input  [4:0] op3,
  output [4:0] op,
  output tworeg,
  output sys,
  output imm5_valid,
  output imm11_valid,
  output rs_valid,
  output rd_valid
);

  wire i11, ri, rr;

  Decoder #(.Selector_Bits(3)) decoder_1 (
    .sel(fmt), .out_0(sys), .out_1(i11), .out_2(rr), .out_3(ri));  // open: out_4, out_5, out_6, out_7
  or or_1 (imm5_valid, ri, fmt[2]);
  or or_2 (imm11_valid, sys, i11);
  or or_3 (tworeg, rr, fmt[2]);
  or or_4 (rs_valid, fmt[2], rr);
  nor nor_1 (rd_valid, sys, i11);
  Multiplexer #(.Selector_Bits(3), .Bits(5)) multiplexer_1 (
    .sel(fmt), .in_0({fmt, op1}), .in_1({fmt, op1}), .in_2(op3), .in_3({1'b1, op2}),
    .in_4({3'b000, fmt[1:0]}), .in_5({3'b000, fmt[1:0]}), .in_6({3'b000, fmt[1:0]}),
    .in_7({3'b000, fmt[1:0]}), .out(op));

  // Other names for the same wires on the sheet: ls = fmt[2]
endmodule
