// Digital circuit memaccess.dig as structural Verilog
module memaccess (
  input  [15:0] result,
  input  [15:0] rdval,
  input  mem,
  input  store,
  input  [15:0] D,
  input  en,
  output [15:0] wrval,
  output [13:0] A,
  output str,
  output [15:0] D_in
);

  Multiplexer #(.Selector_Bits(2), .Bits(16)) multiplexer_1 (
    .sel({mem, store}), .in_0(result), .in_1(result), .in_2(D), .in_3(rdval), .out(wrval));
  and and_1 (str, store, mem, en);

  assign A = result[13:0];
  assign D_in = rdval;
endmodule
