// Digital circuit rddisplay.dig as structural Verilog
module rddisplay (
  input  [25:0] i,
  input  C,
  output [15:0] D1,
  output P1,
  output [15:0] D2,
  output P2,
  output [25:0] o,
  output [15:0] D3,
  output P3
);

  wire decodedec_1_pc, decodedec_1_valid;
  wire [3:0] decodedec_1_r;
  wire [7:0] multiplexer_1_out;
  wire [15:0] debugval_1_q;

  Multiplexer #(.Bits(8)) multiplexer_1 (.sel(C), .in_0(8'h18), .in_1(8'h19), .out(multiplexer_1_out));
  debugval debugval_1 (.db_i(i), .sel(multiplexer_1_out), .db_o(o), .Q(debugval_1_q));
  decodedec decodedec_1 (.D(debugval_1_q), .r(decodedec_1_r), .pc(decodedec_1_pc), .valid(decodedec_1_valid));
  // regdisplay regdisplay_1: pin names not known; wires that end beside it: D1, decodedec_1_r, P1, D2, decodedec_1_pc, P2, D3, decodedec_1_valid, P3
endmodule
