// Digital circuit regfile.dig as structural Verilog
module regfile (
  input  [3:0] rs,
  input  [3:0] rd,
  input  [15:0] wrval,
  input  clock,
  input  en,
  input  wr,
  output [15:0] rdval,
  output [15:0] rsval
);

  wire and_1_out;

  and and_1 (and_1_out, en, wr);
  RegisterFile #(.AddrBits(4), .Bits(16)) registerfile_1 (
    .Din(wrval), .we(and_1_out), .Rw(rd), .C(clock), .Ra(rd), .Rb(rs), .Da(rdval), .Db(rsval));
endmodule
