// Digital circuit rj32.dig as structural Verilog
module rj32 (
  input  clock,
  input  step,
  input  run_slow,
  input  [15:0] D_prog,
  input  [15:0] D_in,
  input  run_fast,
  input  run_faster,
  input  erun,
  input  ack,
  output halt,
  output error,
  output skip,
  output stall,
  output [7:0] A_prog,
  output clock_m,
  output [15:0] A_data,
  output [15:0] D_out,
  output w_en,
  output [25:0] db,
  output req
);

  wire decoder_1_p2, fetch_1_p7, skip_n;
  wire [2:0] aluop_t, cond_t;
  wire [3:0] rd_t, rs_t;
  wire [4:0] fullop_t;
  wire [5:5] rdf_t, rsf_t;
  wire [15:0] decoder_1_p1, execute_1_p5, execute_1_p6, imm_t, L_t, R_t, result_t, writeback_1_rdval_out,
       writeback_1_result_out, wrval_t;
  wire [15:4] ctrl_t;
  wire [15:8] A_prog_t;

  not not_1 (clock_m, clock);
  // fetch fetch_1: pin names not known; wires that end beside it: result_t, D_prog, clock, ctrl_t[11], ctrl_t[4], ctrl_t[12], fetch_1_p7, {A_prog_t, A_prog}
  // decoder decoder_1: pin names not known; wires that end beside it: decoder_1_p1, decoder_1_p2, fetch_1_p7, {A_prog_t, A_prog}, ctrl_t[4], clock, ctrl_t[11], rs_t, rd_t, L_t, R_t, fullop_t, rsf_t[5], rdf_t[5], imm_t, ctrl_t[15]
  clockctrl clockctrl_1 (
    .clock(clock), .step(step), .slow(run_slow), .fast(run_fast), .faster(run_faster), .efast(erun),
    .stall(stall));
  control control_1 (
    .op(fullop_t), .stall(stall), .clock(clock), .skip_n(skip_n), .ack(ack), .aluop(aluop_t), .cond(cond_t),
    .skip(skip), .halt(halt), .error(error), .en_write(ctrl_t[12]), .mem(req), .store(ctrl_t[9]),
    .en_fetch(ctrl_t[11]), .jump(ctrl_t[4]), .write(ctrl_t[10]), .wrmux(ctrl_t[14:13]));
  // execute execute_1: pin names not known; wires that end beside it: L_t, R_t, aluop_t, cond_t, execute_1_p5, execute_1_p6, result_t, skip_n
  writeback writeback_1 (
    .L(execute_1_p5), .R(execute_1_p6), .result(result_t), .rdval(decoder_1_p1), .D(D_in),
    .wrmux(ctrl_t[14:13]), .wrval(wrval_t), .result_out(writeback_1_result_out),
    .rdval_out(writeback_1_rdval_out));
  debugbus debugbus_1 (
    .db_ready(1'b1), .clock(clock), .ctrl({ctrl_t[15:9], req, aluop_t, ctrl_t[4], error, halt, skip, stall}),
    .wrval(wrval_t), .result(result_t), .L(L_t), .R(R_t), .imm(imm_t), .pc({A_prog_t, A_prog}),
    .fullop({{8{1'b0}}, cond_t, fullop_t}), .rdf({{10{1'b0}}, rdf_t[5], ctrl_t[4], rd_t}),
    .rsf({{10{1'b0}}, rsf_t[5], 1'b0, rs_t}), .db(db));
  // memaccess memaccess_1: pin names not known; wires that end beside it: writeback_1_result_out, writeback_1_rdval_out, ctrl_t[9], ctrl_t[12], A_data, w_en, D_out
  // regfile regfile_1: pin names not known; wires that end beside it: rs_t, rd_t, wrval_t, clock, ctrl_t[12], ctrl_t[10], decoder_1_p1, decoder_1_p2

  // Other names for the same wires on the sheet: A_data_t[15:0] = A_data; ack_t = ack;
  //   ctrl_t (some bits) = {req, aluop_t, error, halt, skip, stall}; C = clock; fullop_t[7:5] = cond_t;
  //   D_in_t[15:0] = D_in; D_out_t[15:0] = D_out; D_prog_t[15:0] = D_prog; en = ctrl_t[12]; en_fetch = ctrl_t[11];
  //   error_t = error; halt_t = halt; immv_t = ctrl_t[15]; jump_t = ctrl_t[4]; rdf_t[4:0] = {ctrl_t[4], rd_t};
  //   mem_t = req; op_t[4:0] = fullop_t; A_prog_t[7:0] = A_prog; PC_t[15:0] = {A_prog_t, A_prog};
  //   rdvalid_t = rdf_t[5]; rsf_t[3:0] = rs_t; rsvalid_t = rsf_t[5]; skip_t = skip; stall_t = stall;
  //   store_t = ctrl_t[9]; W_en_t = w_en; write_t = ctrl_t[10]; wrmux_t[1:0] = ctrl_t[14:13]

  // Notes on the sheet:
  //   clock: Hz: 10
  //   rj45 Creates
endmodule
