// Digital circuit rsdisplay.dig as structural Verilog
module rsdisplay (
  input  [25:0] i,
  output [15:0] D1,
  output P1,
  output [15:0] D2,
  output P2,
  output [25:0] o,
  output [15:0] D3,
  output P3
);

  wire decodedec_1_p2, decodedec_1_p3;
  wire [15:0] debugval_1_q;

  debugval debugval_1 (.db_i(i), .sel(8'h10), .db_o(o), .Q(debugval_1_q));
  // decodedec decodedec_1: pin names not known; wires that end beside it: debugval_1_q, decodedec_1_p2, decodedec_1_p3
  // regdisplay regdisplay_1: pin names not known; wires that end beside it: D1, decodedec_1_p2, P1, D2, 1'b0, P2, D3, decodedec_1_p3, P3
endmodule
