// Digital circuit testsuite.dig as structural Verilog
module testsuite (
  input  clock,
  input  run,
  output error,
  output halt,
  output [15:0] PC
);

  // frontpanel frontpanel_1: pin names not known; wires that end beside it: clock, run, 1'b0, PC, halt, error
endmodule

/* Test case jump:
clock run error halt

# #include "../cpudef.asm"
# 
#   jump one
#   error
# three:
#   add r0, r1
#   add r0, r2
#   jump end
#   error
# two:
#   move r2, 2
#   jump three
#   error
# one:
#   move r1, 3
#   jump two
#   error
# end:
#   if.ne r0, 5
#   error
#   halt

program(0x0085, 0x0010, 0x0180, 0x0280, 0x0075, 0x0010, 0x2024, 0xffa5, 0x0010, 0x1034, 0xffb5, 0x0010, 0x02a3, 0x0010, 0x0018)

let i = 0;
while(!(halt | error | (i >= 100)))
  let i = i + 1;
  0 1 0 0
  1 1 x x
end while
0 1 0 1
*/

/* Test case if.eq:
clock run error halt

# #include "../cpudef.asm"
# 
# move r1, 2
# move r2, 3
# move r3, 3
# 
# ; skip r-r
# if.eq r1, r2
# error
# 
# ; skip r-i
# if.eq r1, 3
# error
# 
# ; no-skip r-r
# if.eq r2, r3
# jump p1
# error
# p1:
# 
# ; no-skip r-i
# if.eq r2, 3
# jump p2
# error
# p2:
# 
# halt

program(0x1024, 0x2034, 0x3034, 0x1212, 0x0010, 0x1193, 0x0010, 0x2312, 0x0015, 0x0010, 0x2193, 0x0015, 0x0010, 0x0018)

let i = 0;
while(!(halt | error | (i >= 100)))
  let i = i + 1;
  0 1 0 0
  1 1 x x
end while
0 1 0 1
*/

/* Test case if.lt:
clock run error halt

# #include "../cpudef.asm"
# 
# move r1, -1
# move r2, 0
# 
# ; skip r-r
# if.lt r2, r1
# error
# 
# ; skip r-r equal
# if.lt r2, r2
# error
# 
# ; skip r-i
# if.lt r2, -1
# error
# 
# ; skip r-i equal
# if.lt r2, 0
# error
# 
# ; no-skip r-r
# if.lt r1, r2
# jump p1
# error
# p1:
# 
# ; no-skip r-i
# if.lt r1, 1
# jump p2
# error
# p2:
# 
# halt

program(0x1ff4, 0x2004, 0x2132, 0x0010, 0x2232, 0x0010, 0x2fb3, 0x0010, 0x2033, 0x0010, 0x1232, 0x0015, 0x0010, 0x10b3, 0x0015, 0x0010, 0x0018)

let i = 0;
while(!(halt | error | (i >= 100)))
  let i = i + 1;
  0 1 0 0
  1 1 x x
end while
0 1 0 1
*/

/* Test case if.lo:
clock run error halt

# #include "../cpudef.asm"
# 
# move r1, 0
# move r2, -1 ; 0xffff
# 
# ; skip r-r
# if.lo r2, r1
# error
# 
# ; skip r-r equal
# if.lo r2, r2
# error
# 
# ; skip r-i
# if.lo r2, 0
# error
# 
# ; skip r-i equal
# if.lo r2, -1
# error
# 
# ; no-skip r-r
# if.lo r1, r2
# jump p1
# error
# p1:
# 
# ; no-skip r-i
# if.lo r1, 1
# jump p2
# error
# p2:
# 
# halt

program(0x1004, 0x2ff4, 0x2152, 0x0010, 0x2252, 0x0010, 0x2053, 0x0010, 0x2fd3, 0x0010, 0x1252, 0x0015, 0x0010, 0x10d3, 0x0015, 0x0010, 0x0018)

let i = 0;
while(!(halt | error | (i >= 100)))
  let i = i + 1;
  0 1 0 0
  1 1 x x
end while
0 1 0 1
*/

/* Test case loadstore:
clock run error halt

# #include "../cpudef.asm"
# 
# move r0, 2
# move r1, 5
# 
# ; memory doesn't have 5
# load r2, [r0,0]
# if.eq r2, 5
# error
# 
# ; store and check it does have 5
# store [r0,0], r1
# load r2, [r0,0]
# if.ne r2, 5
# error
# 
# ; check max offset of 31
# move r1, 7
# store [r0,31], r1
# load r2, [r0,31]
# if.ne r2, 7
# error
# 
# ; check base equivalent to offset
# move r2, 0
# add r0, 15
# add r0, 15
# add r0, 1
# load r2, [r0, 0]
# if.ne r2, 7
# error
# 
# ; check multiple writes and reads in a row
# move r1, 1
# move r2, 2
# move r3, 3
# move r4, 4
# move r5, 5
# move r6, 6
# move r0, 0
# store [r0, 3], r3
# store [r0, 1], r1
# store [r0, 6], r6
# store [r0, 2], r2
# store [r0, 4], r4
# store [r0, 5], r5
# move r1, -1
# move r2, -1
# move r3, -1
# move r4, -1
# move r5, -1
# move r6, -1
# load r5, [r0, 5]
# load r1, [r0, 1]
# load r6, [r0, 6]
# load r2, [r0, 2]
# load r4, [r0, 4]
# load r3, [r0, 3]
# if.ne r1, 1
#   error
# if.ne r2, 2
#   error
# if.ne r3, 3
#   error
# if.ne r4, 4
#   error
# if.ne r5, 5
#   error
# if.ne r6, 6
#   error
# 
# halt

program(0x0024, 0x1054, 0x2006, 0x2293, 0x0010, 0x1007, 0x2006, 0x22a3, 0x0010, 0x1074, 0x10ff, 0x20fe, 0x23a3, 0x0010, 0x2004, 0x03c1, 0x03c1, 0x0041, 0x2006, 0x23a3, 0x0010, 0x1014, 0x2024, 0x3034, 0x4044, 0x5054, 0x6064, 0x0004, 0x301f, 0x100f, 0x6037, 0x2017, 0x4027, 0x502f, 0x1ff4, 0x2ff4, 0x3ff4, 0x4ff4, 0x5ff4, 0x6ff4, 0x502e, 0x100e, 0x6036, 0x2016, 0x4026, 0x301e, 0x10a3, 0x0010, 0x2123, 0x0010, 0x31a3, 0x0010, 0x4223, 0x0010, 0x52a3, 0x0010, 0x6323, 0x0010, 0x0018)

let i = 0;
while(!(halt | error | (i >= 100)))
  let i = i + 1;
  0 1 0 0
  1 1 x x
end while
0 1 0 1
*/

/* Test case if.ne:
clock run error halt

# #include "../cpudef.asm"
# 
# move r1, 2
# move r2, 3
# move r3, 3
# 
# ; skip r-r
# if.ne r2, r2
# error
# 
# ; skip r-i
# if.ne r1, 2
# error
# 
# ; no-skip r-r
# if.ne r2, r1
# jump p1
# error
# p1:
# 
# ; no-skip r-i
# if.ne r2, 2
# jump p2
# error
# p2:
# 
# halt

program(0x1024, 0x2034, 0x3034, 0x2222, 0x0010, 0x1123, 0x0010, 0x2122, 0x0015, 0x0010, 0x2123, 0x0015, 0x0010, 0x0018)

let i = 0;
while(!(halt | error | (i >= 100)))
  let i = i + 1;
  0 1 0 0
  1 1 x x
end while
0 1 0 1
*/

/* Test case if.ge:
clock run error halt

# #include "../cpudef.asm"
# 
# move r1, -1
# move r2, 0
# 
# ; skip r-r
# if.ge r1, r2
# error
# 
# ; skip r-i
# if.ge r1, 0
# error
# 
# ; no-skip r-r
# if.ge r2, r1
# jump p1
# error
# p1:
# 
# ; no-skip r-r equal
# if.ge r2, r2
# jump p2
# error
# p2:
# 
# ; no-skip r-i
# if.ge r2, 0
# jump p3
# error
# p3:
# 
# ; no-skip r-i equal
# if.ge r1, -1
# jump p4
# error
# p4:
# 
# halt

program(0x1ff4, 0x2004, 0x1242, 0x0010, 0x1043, 0x0010, 0x2142, 0x0015, 0x0010, 0x2242, 0x0015, 0x0010, 0x2043, 0x0015, 0x0010, 0x1fc3, 0x0015, 0x0010, 0x0018)

let i = 0;
while(!(halt | error | (i >= 100)))
  let i = i + 1;
  0 1 0 0
  1 1 x x
end while
0 1 0 1
*/

/* Test case if.hs:
clock run error halt

# #include "../cpudef.asm"
# 
# move r1, 0
# move r2, -1 ; 0xffff
# 
# ; skip r-r
# if.hs r1, r2
# error
# 
# ; skip r-i
# if.hs r1, -1
# error
# 
# ; no-skip r-r
# if.hs r2, r1
# jump p1
# error
# p1:
# 
# ; no-skip r-r equal
# if.hs r2, r2
# jump p2
# error
# p2:
# 
# ; no-skip r-i
# if.hs r2, -1
# jump p3
# error
# p3:
# 
# ; no-skip r-i equal
# if.hs r1, 0
# jump p4
# error
# p4:
# 
# halt

program(0x1004, 0x2ff4, 0x1262, 0x0010, 0x1fe3, 0x0010, 0x2162, 0x0015, 0x0010, 0x2262, 0x0015, 0x0010, 0x2fe3, 0x0015, 0x0010, 0x1063, 0x0015, 0x0010, 0x0018)

let i = 0;
while(!(halt | error | (i >= 100)))
  let i = i + 1;
  0 1 0 0
  1 1 x x
end while
0 1 0 1
*/

/* Test case add:
clock run error halt

# #include "../cpudef.asm"
# 
# move r1, 5
# move r2, 3
# add r1, r2
# add r1, 2
# if.ne r1, 10
# error
# halt

program(0x1054, 0x2034, 0x1280, 0x1081, 0x1523, 0x0010, 0x0018)

let i = 0;
while(!(halt | error | (i >= 100)))
  let i = i + 1;
  0 1 0 0
  1 1 x x
end while
0 1 0 1
*/

/* Test case sub:
clock run error halt

# #include "../cpudef.asm"
# 
# move r1, 5
# move r2, 3
# sub r1, r2
# if.ne r1, 2
#   error
# 
# sub r1, 2
# if.ne r1, 0
#   error
# halt

program(0x1054, 0x2034, 0x1288, 0x1123, 0x0010, 0x1089, 0x1023, 0x0010, 0x0018)

let i = 0;
while(!(halt | error | (i >= 100)))
  let i = i + 1;
  0 1 0 0
  1 1 x x
end while
0 1 0 1
*/

/* Test case xor:
clock run error halt

# #include "../cpudef.asm"
# 
# move r1,  0b110
# move r2,  0b010
# 
# xor r1, r2
# if.ne r1, 0b100
#   error
# 
# xor r1, r2
# if.ne r1, 0b110
#   error
# 
# xor r1,   0b011
# if.ne r1, 0b101
#   error
# 
# halt

program(0x1064, 0x2024, 0x1290, 0x1223, 0x0010, 0x1290, 0x1323, 0x0010, 0x10d1, 0x12a3, 0x0010, 0x0018)

let i = 0;
while(!(halt | error | (i >= 100)))
  let i = i + 1;
  0 1 0 0
  1 1 x x
end while
0 1 0 1
*/

/* Test case and:
clock run error halt

# #include "../cpudef.asm"
# 
# move r1,  0b0110
# move r2,  0b1010
# 
# and r1, r2
# if.ne r1, 0b0010
#   error
# 
# and r2,   0b1101
# if.ne r2, 0b1000
#   error
# 
# halt

program(0x1064, 0x20a4, 0x1298, 0x1123, 0x0010, 0x2359, 0x2423, 0x0010, 0x0018)

let i = 0;
while(!(halt | error | (i >= 100)))
  let i = i + 1;
  0 1 0 0
  1 1 x x
end while
0 1 0 1
*/

/* Test case or:
clock run error halt

# #include "../cpudef.asm"
# 
# move r1,  0b0110
# move r2,  0b1010
# 
# or r1, r2
# if.ne r1, 0b1110
#   error
# 
# or r2,   0b0001
# if.ne r2, 0b1011
#   error
# 
# halt

program(0x1064, 0x20a4, 0x12a0, 0x1723, 0x0010, 0x2061, 0x25a3, 0x0010, 0x0018)

let i = 0;
while(!(halt | error | (i >= 100)))
  let i = i + 1;
  0 1 0 0
  1 1 x x
end while
0 1 0 1
*/

/* Test case call:
clock run error halt

# #include "../cpudef.asm"
# 
# call test
# if.ne r1, 5
#   error
# halt
# 
# error
# test:
#   move r1, 5
#   jump r0
# 
# error
# halt

program(0x004d, 0x12a3, 0x0010, 0x0018, 0x0010, 0x1054, 0x0020, 0x0010, 0x0018)

let i = 0;
while(!(halt | error | (i >= 100)))
  let i = i + 1;
  0 1 0 0
  1 1 x x
end while
0 1 0 1
*/

/* Test case shl:
clock run error halt

# #include "../cpudef.asm"
# 
# move r1,  0b011
# move r2,  0
# move r3,  1
# move r4,  2
# 
# shl r1, 0
# if.ne r1, 0b011
#   error
# 
# shl r1, r2
# if.ne r1, 0b011
#   error
# 
# shl r1, 1
# if.ne r1, 0b110
#   error
# 
# shl r1, r3
# if.ne r1, 0b1100
#   error
# 
# move r1,  0b011
# 
# shl r1, 2
# if.ne r1, 0b1100
#   error
# 
# move r1,  0b011
# 
# shl r1, r4
# if.ne r1, 0b1100
#   error
# 
# halt

program(0x1034, 0x2004, 0x3014, 0x4024, 0x1029, 0x11a3, 0x0010, 0x12a8, 0x11a3, 0x0010, 0x1069, 0x1323, 0x0010, 0x13a8, 0x1623, 0x0010, 0x1034, 0x10a9, 0x1623, 0x0010, 0x1034, 0x14a8, 0x1623, 0x0010, 0x0018)

let i = 0;
while(!(halt | error | (i >= 100)))
  let i = i + 1;
  0 1 0 0
  1 1 x x
end while
0 1 0 1
*/

/* Test case shr:
clock run error halt

# #include "../cpudef.asm"
# 
# move r1,  0b110
# move r2,  0
# move r3,  1
# move r4,  2
# 
# shr r1, 0
# if.ne r1, 0b110
#   error
# 
# shr r1, r2
# if.ne r1, 0b110
#   error
# 
# shr r1, 1
# if.ne r1, 0b011
#   error
# 
# shr r1, r3
# if.ne r1, 0b001
#   error
# 
# move r1,  0b1100
# 
# shr r1, 2
# if.ne r1, 0b0011
#   error
# 
# move r1,  0b1100
# 
# shr r1, r4
# if.ne r1, 0b0011
#   error
# 
# move r1, -42
# shr r1, 2
# if.eq r1, -10
#   error
# 
# halt

program(0x1064, 0x2004, 0x3014, 0x4024, 0x1031, 0x1323, 0x0010, 0x12b0, 0x1323, 0x0010, 0x1071, 0x11a3, 0x0010, 0x13b0, 0x10a3, 0x0010, 0x10c4, 0x10b1, 0x11a3, 0x0010, 0x10c4, 0x14b0, 0x11a3, 0x0010, 0x1d64, 0x10b1, 0x1b13, 0x0010, 0x0018)

let i = 0;
while(!(halt | error | (i >= 100)))
  let i = i + 1;
  0 1 0 0
  1 1 x x
end while
0 1 0 1
*/

/* Test case asr:
clock run error halt

# #include "../cpudef.asm"
# 
# move r1,  0b110
# move r2,  0
# move r3,  1
# move r4,  2
# 
# asr r1, 0
# if.ne r1, 0b110
#   error
# 
# asr r1, r2
# if.ne r1, 0b110
#   error
# 
# asr r1, 1
# if.ne r1, 0b011
#   error
# 
# asr r1, r3
# if.ne r1, 0b001
#   error
# 
# move r1,  0b1100
# 
# asr r1, 2
# if.ne r1, 0b0011
#   error
# 
# move r1,  0b1100
# 
# asr r1, r4
# if.ne r1, 0b0011
#   error
# 
# move r1, -8
# asr r1, 2
# if.ne r1, -2
#   error
# 
# asr r1, 2
# if.ne r1, -1
#   error
# 
# move r1, -10
# asr r1, 1
# if.ne r1, -5
#   error
# 
# halt

program(0x1064, 0x2004, 0x3014, 0x4024, 0x1039, 0x1323, 0x0010, 0x12b8, 0x1323, 0x0010, 0x1079, 0x11a3, 0x0010, 0x13b8, 0x10a3, 0x0010, 0x10c4, 0x10b9, 0x11a3, 0x0010, 0x10c4, 0x14b8, 0x11a3, 0x0010, 0x1f84, 0x10b9, 0x1f23, 0x0010, 0x10b9, 0x1fa3, 0x0010, 0x1f64, 0x1079, 0x1da3, 0x0010, 0x0018)

let i = 0;
while(!(halt | error | (i >= 100)))
  let i = i + 1;
  0 1 0 0
  1 1 x x
end while
0 1 0 1
*/
