// Digital circuit engine.dig as structural Verilog
module engine (
  input  clk,
  input  rst,
  input  [11:0] x_i,
  input  [11:0] y_i,
  input  nl_i,
  input  nf_i,
  input  hs_i,
  input  vs_i,
  input  de_i,
  output [11:0] x_o,
  output [11:0] y_o,
  output nl_o,
  output nf_o,
  output [7:0] r,
  output [7:0] g,
  output [7:0] b,
  output hs_o,
  output vs_o,
  output de_o
);

  wire [7:0] demultiplexer_1_out_0, demultiplexer_1_out_1, demultiplexer_1_out_2, demultiplexer_1_out_3,
       or_1_out, or_2_out, or_3_out;

  Demultiplexer #(.Selector_Bits(2), .Bits(8)) demultiplexer_1 (
    .sel(y_i[7:6]), .in(x_i[8:1]), .out_0(demultiplexer_1_out_0), .out_1(demultiplexer_1_out_1),
    .out_2(demultiplexer_1_out_2), .out_3(demultiplexer_1_out_3));
  assign or_1_out = demultiplexer_1_out_0 | demultiplexer_1_out_3;  // Or or_1, 8 bits wide
  assign or_2_out = demultiplexer_1_out_1 | demultiplexer_1_out_3;  // Or or_2, 8 bits wide
  assign or_3_out = demultiplexer_1_out_2 | demultiplexer_1_out_3;  // Or or_3, 8 bits wide
  Multiplexer #(.Bits(8)) multiplexer_1 (.sel(de_i), .in_0({8{1'b0}}), .in_1(or_1_out), .out(r));
  Multiplexer #(.Bits(8)) multiplexer_2 (.sel(de_i), .in_0({8{1'b0}}), .in_1(or_2_out), .out(g));
  Multiplexer #(.Bits(8)) multiplexer_3 (.sel(de_i), .in_0({8{1'b0}}), .in_1(or_3_out), .out(b));

  assign de_o = de_i;
  assign hs_o = hs_i;
  assign nf_o = nf_i;
  assign nl_o = nl_i;
  assign vs_o = vs_i;
  assign x_o = x_i;
  assign y_o = y_i;
endmodule
