// Digital circuit sync.dig as structural Verilog
module sync (
  input  en,
  input  [11:0] v,
  input  [11:0] fp,
  input  [11:0] sync,
  input  [11:0] bp,
  output blank_bgn,
  output sync_bgn,
  output sync_end
);

  wire equals_1_q, equals_2_q, equals_3_q;

  equals #(.generic("bitWidth := 12;")) equals_1 (.A(v), .B(fp), .Q(equals_1_q));
  equals #(.generic("bitWidth := 12;")) equals_2 (.A(v), .B(sync), .Q(equals_2_q));
  equals #(.generic("bitWidth := 12;")) equals_3 (.A(v), .B(bp), .Q(equals_3_q));
  and and_1 (blank_bgn, en, equals_1_q);
  and and_2 (sync_bgn, en, equals_2_q);
  and and_3 (sync_end, en, equals_3_q);

  // Notes on the sheet:
  //   fp: default 3
  //   sync: default 5
  //   bp: default 7
endmodule
