// Digital circuit top_simfb.dig as structural Verilog
module top_simfb (
  input  clk,
  input  rst
);

  wire scanxy_1_p8, scanxy_1_p9;
  wire [7:0] engine_1_b, engine_1_g, engine_1_r;
  wire [11:0] engine_1_x_o, engine_1_y_o, scanxy_1_p6, scanxy_1_p7;

  // scanxy scanxy_1: pin names not known; wires that end beside it: clk, rst, 1'b1, 12'h280, 12'h168, scanxy_1_p6, scanxy_1_p7, scanxy_1_p8, scanxy_1_p9
  engine engine_1 (
    .clk(clk), .rst(rst), .x_i(scanxy_1_p6), .y_i(scanxy_1_p7), .line_i(scanxy_1_p8), .frame_i(scanxy_1_p9),
    .hsync_i(1'b0), .vsync_i(1'b0), .en_disp_i(1'b1), .x_o(engine_1_x_o), .y_o(engine_1_y_o), .r(engine_1_r),
    .g(engine_1_g), .b(engine_1_b));  // open: line_o, frame_o, hsync_o, vsync_o, en_disp_o
  // framebuffer framebuffer_1: pin names not known; wires that end beside it: clk, engine_1_x_o, engine_1_y_o, engine_1_r, engine_1_g, engine_1_b

  // Other names for the same wires on the sheet: C = clk; R = rst

  // Notes on the sheet:
  //   clk: Hz: 2147483647
endmodule
