// Digital circuit vdp.dig as structural Verilog
module vdp (
  input  clk,
  input  rst,
  input  [11:0] h_fp,
  input  [11:0] h_sync,
  input  [11:0] h_bp,
  input  [11:0] h_total,
  input  h_neg,
  input  [11:0] v_fp,
  input  [11:0] v_sync,
  input  [11:0] v_bp,
  input  [11:0] v_total,
  input  v_neg,
  output [7:0] r,
  output [7:0] g,
  output [7:0] b,
  output hsync,
  output vsync,
  output en_disp,
  output [11:0] x,
  output [11:0] y,
  output line,
  output frame
);

  wire undriven_3, undriven_4, vgasync_1_en_disp, vgasync_1_frame_o, vgasync_1_hsync, vgasync_1_line_o,
       vgasync_1_vsync;
  wire [11:0] undriven, undriven_2, vgasync_1_x_o, vgasync_1_y_o;

  scanxy scanxy_1 (.C(clk), .rst(rst), .en(1'b1), .hr(h_total), .vr(v_total));  // open: X, Y, nl, nf
  vgasync vgasync_1 (
    .clk(clk), .rst(rst), .x_i(undriven), .y_i(undriven_2), .line_i(undriven_3), .frame_i(undriven_4),
    .h_fp(h_fp), .h_sync(h_sync), .h_bp(h_bp), .h_neg(h_neg), .v_fp(v_fp), .v_sync(v_sync), .v_bp(v_bp),
    .v_neg(v_neg), .x_o(vgasync_1_x_o), .y_o(vgasync_1_y_o), .line_o(vgasync_1_line_o),
    .frame_o(vgasync_1_frame_o), .hsync(vgasync_1_hsync), .vsync(vgasync_1_vsync), .en_disp(vgasync_1_en_disp));
  engine engine_1 (
    .clk(clk), .rst(rst), .x_i(vgasync_1_x_o), .y_i(vgasync_1_y_o), .line_i(vgasync_1_line_o),
    .frame_i(vgasync_1_frame_o), .hsync_i(vgasync_1_hsync), .vsync_i(vgasync_1_vsync),
    .en_disp_i(vgasync_1_en_disp), .x_o(x), .y_o(y), .line_o(line), .frame_o(frame), .r(r), .g(g), .b(b),
    .hsync_o(hsync), .vsync_o(vsync), .en_disp_o(en_disp));

  // Other names for the same wires on the sheet: C = clk; R_t = rst

  // Notes on the sheet:
  //   clk: Hz: 2147483647
  //   h_fp: default 3
  //   h_sync: default 5
  //   h_bp: default 5
  //   v_fp: default 3
  //   v_sync: default 5
  //   v_bp: default 5
endmodule
