// Digital circuit vgasync.dig as structural Verilog
module vgasync (
  input  clk,
  input  rst,
  input  [11:0] X_i,
  input  [11:0] Y_i,
  input  nl_i,
  input  nf_i,
  input  [11:0] hfp,
  input  [11:0] hsn,
  input  [11:0] hbp,
  input  hneg,
  input  [11:0] vfp,
  input  [11:0] vsn,
  input  [11:0] vbp,
  input  vneg,
  output [11:0] X_o,
  output [11:0] Y_o,
  output nl_o,
  output nf_o,
  output hs,
  output vs,
  output de
);

  wire H_b, V_b;

  sync H (.clk(clk), .rst(rst), .v(X_i), .fp(hfp), .sn(hsn), .bp(hbp), .n(nl_i), .neg(hneg), .b(H_b), .s(hs));
  sync V (.clk(clk), .rst(rst), .v(Y_i), .fp(vfp), .sn(vsn), .bp(vbp), .n(nf_i), .neg(vneg), .b(V_b), .s(vs));
  nor nor_1 (de, H_b, V_b);

  assign nf_o = nf_i;
  assign nl_o = nl_i;
  assign X_o = X_i;
  assign Y_o = Y_i;

  // Other names for the same wires on the sheet: C = clk; nf_t = nf_i; nl_t = nl_i; R = rst; X_t[11:0] = X_i;
  //   Y_t[11:0] = Y_i

  // Notes on the sheet:
  //   hfp: default 3
  //   hsn: default 5
  //   hbp: default 5
  //   vfp: default 3
  //   vsn: default 5
  //   vbp: default 5
endmodule
