// Digital circuit vga_aluopdisp.dig as structural Verilog
module vga_aluopdisp (
  input  [15:0] aluop,
  input  [2:0] digit,
  output [6:0] char
);

  wire [6:0] aluop2ascii_1_l0, aluop2ascii_1_l1, aluop2ascii_1_l2, aluop2ascii_1_l3;

  aluop2ascii aluop2ascii_1 (
    .I({1'b0, aluop[7:5]}), .L0(aluop2ascii_1_l0), .L1(aluop2ascii_1_l1), .L2(aluop2ascii_1_l2),
    .L3(aluop2ascii_1_l3));  // open: L_v, R_v, res_v
  Multiplexer #(.Selector_Bits(2), .Bits(7)) multiplexer_1 (
    .sel(digit[1:0]), .in_0(aluop2ascii_1_l0), .in_1(aluop2ascii_1_l1), .in_2(aluop2ascii_1_l2),
    .in_3(aluop2ascii_1_l3), .out(char));
endmodule
