// Digital circuit vga_blinkenlights.dig as structural Verilog
module vga_blinkenlights (
  input  clock,
  input  [15:0] PC,
  input  [15:0] R0,
  input  [15:0] R1,
  input  [15:0] R2,
  input  [15:0] R3,
  input  [15:0] L_b,
  input  [15:0] R_b,
  input  [15:0] result,
  input  skip,
  input  jump,
  input  [4:0] op,
  input  [2:0] cond,
  input  [15:0] CD,
  input  clock_slow,
  output [3:0] R,
  output [3:0] G,
  output [3:0] B,
  output hs,
  output vs,
  output de,
  output [10:0] CA
);

  wire jump_t, register_9_q, register_10_q, skip_t;
  wire [2:0] cond_t, register_12_q;
  wire [4:0] op_t, register_11_q;
  wire [6:0] jump_c_o, L_c_o, Op_c_o, PC_c_o, R0_c_o, R1_c_o, R2_c_o, R3_c_o, R_c_o, result_c_o, skip_c_o;
  wire [7:0] jump_cx_o, jump_cy_o, L_cx_o, L_cy_o, Op_cx_o, Op_cy_o, PC_cx_o, PC_cy_o, R0_cx_o, R0_cy_o,
       R1_cx_o, R1_cy_o, R2_cx_o, R2_cy_o, R3_cx_o, R3_cy_o, R_cx_o, R_cy_o, result_cx_o, result_cy_o,
       vga_display_1_cx, vga_display_1_cy;
  wire [11:0] jump_bg_o, jump_fg_o, L_bg_o, L_fg_o, Op_bg_o, Op_fg_o, PC_bg_o, PC_fg_o, R0_bg_o, R0_fg_o,
       R1_bg_o, R1_fg_o, R2_bg_o, R2_fg_o, R3_bg_o, R3_fg_o, R_bg_o, R_fg_o, result_bg_o, result_fg_o,
       skip_bg_o, skip_fg_o;
  wire [15:0] L_t, PC_t, R0_t, R1_t, R2_t, R3_t, R_t, register_1_q, register_2_q, register_3_q, register_4_q,
       register_5_q, register_6_q, register_7_q, register_8_q, result_t;

  Register #(.Bits(16)) register_1 (.D(PC), .C(clock_slow), .en(1'b1), .Q(register_1_q));
  Register #(.Bits(16)) register_2 (.D(R0), .C(clock_slow), .en(1'b1), .Q(register_2_q));
  Register #(.Bits(16)) register_3 (.D(R1), .C(clock_slow), .en(1'b1), .Q(register_3_q));
  Register #(.Bits(16)) register_4 (.D(R2), .C(clock_slow), .en(1'b1), .Q(register_4_q));
  Register #(.Bits(16)) register_5 (.D(R3), .C(clock_slow), .en(1'b1), .Q(register_5_q));
  Register #(.Bits(16)) register_6 (.D(L_b), .C(clock_slow), .en(1'b1), .Q(register_6_q));
  Register #(.Bits(16)) register_7 (.D(R_b), .C(clock_slow), .en(1'b1), .Q(register_7_q));
  Register #(.Bits(16)) register_8 (.D(result), .C(clock_slow), .en(1'b1), .Q(register_8_q));
  Register register_9 (.D(skip), .C(clock_slow), .en(1'b1), .Q(register_9_q));
  Register register_10 (.D(jump), .C(clock_slow), .en(1'b1), .Q(register_10_q));
  Register #(.Bits(5)) register_11 (.D(op), .C(clock_slow), .en(1'b1), .Q(register_11_q));
  Register #(.Bits(3)) register_12 (.D(cond), .C(clock_slow), .en(1'b1), .Q(register_12_q));
  Register #(.Bits(16)) register_13 (.D(register_1_q), .C(clock), .en(1'b1), .Q(PC_t));
  Register #(.Bits(16)) register_14 (.D(register_2_q), .C(clock), .en(1'b1), .Q(R0_t));
  Register #(.Bits(16)) register_15 (.D(register_3_q), .C(clock), .en(1'b1), .Q(R1_t));
  Register #(.Bits(16)) register_16 (.D(register_4_q), .C(clock), .en(1'b1), .Q(R2_t));
  Register #(.Bits(16)) register_17 (.D(register_5_q), .C(clock), .en(1'b1), .Q(R3_t));
  Register #(.Bits(16)) register_18 (.D(register_6_q), .C(clock), .en(1'b1), .Q(L_t));
  Register #(.Bits(16)) register_19 (.D(register_7_q), .C(clock), .en(1'b1), .Q(R_t));
  Register #(.Bits(16)) register_20 (.D(register_8_q), .C(clock), .en(1'b1), .Q(result_t));
  Register register_21 (.D(register_9_q), .C(clock), .en(1'b1), .Q(skip_t));
  Register register_22 (.D(register_10_q), .C(clock), .en(1'b1), .Q(jump_t));
  Register #(.Bits(5)) register_23 (.D(register_11_q), .C(clock), .en(1'b1), .Q(op_t));
  Register #(.Bits(3)) register_24 (.D(register_12_q), .C(clock), .en(1'b1), .Q(cond_t));
  vga_display vga_display_1 (
    .clock(clock), .res_H(12'h280), .fp_H(12'h10), .sync_H(12'h60), .bp_H(12'h30), .neg_H(1'b1),
    .res_V(12'h1e0), .fp_V(12'ha), .sync_V(12'h2), .bp_V(12'h22), .neg_V(1'b1), .char(skip_c_o),
    .fg(skip_fg_o), .bg(skip_bg_o), .CD(CD), .R(R), .G(G), .B(B), .hs(hs), .vs(vs), .de(de),
    .CX(vga_display_1_cx), .CY(vga_display_1_cy), .CA(CA));  // open: vblank, hblank
  vga_labelnum L (
    .CX_i(R3_cx_o), .CY_i(R3_cy_o), .C_i(R3_c_o), .fg_i(R3_fg_o), .bg_i(R3_bg_o), .fg_lab(12'h1be),
    .fg_num(12'he07), .bg_c(12'h112), .CX_c({5{1'b0}}), .CY_c(8'h8), .en(1'b1), .L_0(7'b0100000),
    .L_1(7'b0100000), .L_2(7'b1001100), .N(L_t), .CX_o(L_cx_o), .CY_o(L_cy_o), .C_o(L_c_o), .fg_o(L_fg_o),
    .bg_o(L_bg_o));  // open: busy
  vga_opdisp u_Op (
    .CX_i(L_cx_o), .CY_i(L_cy_o), .C_i(L_c_o), .fg_i(L_fg_o), .bg_i(L_bg_o), .fg_c(12'h1be), .bg_c(12'h112),
    .CX_c(5'b00001), .CY_c(8'h8), .en(1'b1), .op(op_t), .cond(cond_t), .CX_o(Op_cx_o), .CY_o(Op_cy_o),
    .C_o(Op_c_o), .fg_o(Op_fg_o), .bg_o(Op_bg_o));  // open: busy
  vga_labelnum u_PC (
    .CX_i(vga_display_1_cx), .CY_i(vga_display_1_cy), .C_i({7{1'b0}}), .fg_i({12{1'b0}}), .bg_i({12{1'b0}}),
    .fg_lab(12'h1be), .fg_num(12'he07), .bg_c(12'h112), .CX_c({5{1'b0}}), .CY_c(8'h5), .en(1'b1),
    .L_0(7'b0100000), .L_1(7'b1010000), .L_2(7'b1000011), .N(PC_t), .CX_o(PC_cx_o), .CY_o(PC_cy_o),
    .C_o(PC_c_o), .fg_o(PC_fg_o), .bg_o(PC_bg_o));  // open: busy
  vga_labelnum u_R (
    .CX_i(Op_cx_o), .CY_i(Op_cy_o), .C_i(Op_c_o), .fg_i(Op_fg_o), .bg_i(Op_bg_o), .fg_lab(12'h1be),
    .fg_num(12'he07), .bg_c(12'h112), .CX_c(5'b00010), .CY_c(8'h8), .en(1'b1), .L_0(7'b0100000),
    .L_1(7'b0100000), .L_2(7'b1010010), .N(R_t), .CX_o(R_cx_o), .CY_o(R_cy_o), .C_o(R_c_o), .fg_o(R_fg_o),
    .bg_o(R_bg_o));  // open: busy
  vga_labelnum u_R0 (
    .CX_i(PC_cx_o), .CY_i(PC_cy_o), .C_i(PC_c_o), .fg_i(PC_fg_o), .bg_i(PC_bg_o), .fg_lab(12'h1be),
    .fg_num(12'he07), .bg_c(12'h112), .CX_c(5'b00011), .CY_c(8'h2), .en(1'b1), .L_0(7'b0100000),
    .L_1(7'b1010010), .L_2(7'b0110000), .N(R0_t), .CX_o(R0_cx_o), .CY_o(R0_cy_o), .C_o(R0_c_o),
    .fg_o(R0_fg_o), .bg_o(R0_bg_o));  // open: busy
  vga_labelnum u_result (
    .CX_i(R_cx_o), .CY_i(R_cy_o), .C_i(R_c_o), .fg_i(R_fg_o), .bg_i(R_bg_o), .fg_lab(12'h1be),
    .fg_num(12'he07), .bg_c(12'h112), .CX_c(5'b00011), .CY_c(8'h8), .en(1'b1), .L_0(7'b0100000),
    .L_1(7'b0111101), .L_2(7'b0100000), .N(result_t), .CX_o(result_cx_o), .CY_o(result_cy_o),
    .C_o(result_c_o), .fg_o(result_fg_o), .bg_o(result_bg_o));  // open: busy
  vga_labelnum u_R1 (
    .CX_i(R0_cx_o), .CY_i(R0_cy_o), .C_i(R0_c_o), .fg_i(R0_fg_o), .bg_i(R0_bg_o), .fg_lab(12'h1be),
    .fg_num(12'he07), .bg_c(12'h112), .CX_c(5'b00011), .CY_c(8'h3), .en(1'b1), .L_0(7'b0100000),
    .L_1(7'b1010010), .L_2(7'b0110001), .N(R1_t), .CX_o(R1_cx_o), .CY_o(R1_cy_o), .C_o(R1_c_o),
    .fg_o(R1_fg_o), .bg_o(R1_bg_o));  // open: busy
  vga_string u_jump (
    .CX_i(result_cx_o), .CY_i(result_cy_o), .C_i(result_c_o), .fg_i(result_fg_o), .bg_i(result_bg_o),
    .fg_c(12'h1be), .bg_c(12'h112), .CX_c(6'b000001), .CY_c(8'h4), .C_0(7'b1001010), .C_1(7'b1010101),
    .C_2(7'b1001101), .C_3(7'b1010000), .en(jump_t), .CX_o(jump_cx_o), .CY_o(jump_cy_o), .C_o(jump_c_o),
    .fg_o(jump_fg_o), .bg_o(jump_bg_o));
  vga_labelnum u_R2 (
    .CX_i(R1_cx_o), .CY_i(R1_cy_o), .C_i(R1_c_o), .fg_i(R1_fg_o), .bg_i(R1_bg_o), .fg_lab(12'h1be),
    .fg_num(12'he07), .bg_c(12'h112), .CX_c(5'b00011), .CY_c(8'h4), .en(1'b1), .L_0(7'b0100000),
    .L_1(7'b1010010), .L_2(7'b0110010), .N(R2_t), .CX_o(R2_cx_o), .CY_o(R2_cy_o), .C_o(R2_c_o),
    .fg_o(R2_fg_o), .bg_o(R2_bg_o));  // open: busy
  vga_string u_skip (
    .CX_i(jump_cx_o), .CY_i(jump_cy_o), .C_i(jump_c_o), .fg_i(jump_fg_o), .bg_i(jump_bg_o), .fg_c(12'h1be),
    .bg_c(12'h112), .CX_c(6'b000001), .CY_c(8'h3), .C_0(7'b1010011), .C_1(7'b1001011), .C_2(7'b1001001),
    .C_3(7'b1010000), .en(skip_t), .C_o(skip_c_o), .fg_o(skip_fg_o), .bg_o(skip_bg_o));  // open: CX_o, CY_o
  vga_labelnum u_R3 (
    .CX_i(R2_cx_o), .CY_i(R2_cy_o), .C_i(R2_c_o), .fg_i(R2_fg_o), .bg_i(R2_bg_o), .fg_lab(12'h1be),
    .fg_num(12'he07), .bg_c(12'h112), .CX_c(5'b00011), .CY_c(8'h5), .en(1'b1), .L_0(7'b0100000),
    .L_1(7'b1010010), .L_2(7'b0110011), .N(R3_t), .CX_o(R3_cx_o), .CY_o(R3_cy_o), .C_o(R3_c_o),
    .fg_o(R3_fg_o), .bg_o(R3_bg_o));  // open: busy

  // Other names for the same wires on the sheet: C = clock; RC = clock_slow

  // Notes on the sheet:
  //   clock: Hz: 2147483647
endmodule
