// Digital circuit vga_display.dig as structural Verilog
module vga_display (
  input  clock,
  input  [11:0] res_H,
  input  [11:0] fp_H,
  input  [11:0] sync_H,
  input  [11:0] bp_H,
  input  neg_H,
  input  [11:0] res_V,
  input  [11:0] fp_V,
  input  [11:0] sync_V,
  input  [11:0] bp_V,
  input  neg_V,
  input  [6:0] char,
  input  [3:0] fg,
  input  [11:0] bg,
  input  [15:0] CD,
  input  [15:0] PD,
  output [3:0] R,
  output [3:0] G,
  output [3:0] B,
  output hs,
  output vs,
  output de,
  output [7:0] CX,
  output [7:0] CY,
  output [10:0] CA,
  output vblank,
  output hblank,
  output [7:0] PA
);

  wire vga_sync_1_h, vga_sync_1_pic, vga_sync_1_v;
  wire [3:0] vga_charpos_1_col;
  wire [4:0] vga_charpos_1_row;
  wire [11:0] vga_sync_1_x, vga_sync_1_y;

  vga_sync vga_sync_1 (
    .clock(clock), .res_H(res_H), .fp_H(bp_H), .sync_H(sync_H), .bp_H(fp_H), .neg_H(neg_H), .res_V(res_V),
    .fp_V(bp_V), .sync_V(sync_V), .bp_V(fp_V), .neg_V(neg_V), .H(vga_sync_1_h), .V(vga_sync_1_v),
    .pic(vga_sync_1_pic), .X(vga_sync_1_x), .Y(vga_sync_1_y), .vblank(vblank), .hblank(hblank));
  vga_charpos vga_charpos_1 (
    .X(vga_sync_1_x), .Y(vga_sync_1_y), .row(vga_charpos_1_row), .col(vga_charpos_1_col), .CX(CX), .CY(CY));
  // vga_text vga_text_1: pin names not known; wires that end beside it: vga_sync_1_h, vga_sync_1_v, vga_sync_1_pic, vga_charpos_1_row, vga_charpos_1_col, CD, clock, char, fg, bg, PD, R, G, B, hs, vs, de, CA, PA

  // Other names for the same wires on the sheet: C = clock

  // Notes on the sheet:
  //   clock: Hz: 2147483647
  //   res_H: default 640
  //   fp_H: default 16
  //   sync_H: default 96
  //   bp_H: default 48
  //   res_V: default 640
  //   fp_V: default 16
  //   sync_V: default 96
  //   bp_V: default 48
endmodule
