// Digital circuit vga_hex.dig as structural Verilog
module vga_hex (
  input  [7:0] CX_i,
  input  [7:0] CY_i,
  input  [6:0] C_i,
  input  [3:0] fg_i,
  input  [3:0] fg_c,
  input  [5:0] CX_c,
  input  [7:0] CY_c,
  input  [15:0] N,
  input  en,
  output [7:0] CX_o,
  output [7:0] CY_o,
  output [6:0] C_o,
  output [3:0] fg_o
);

  wire [6:0] bcd2ascii_1_d0, bcd2ascii_1_d1, bcd2ascii_1_d2, bcd2ascii_1_d3;

  bcd2ascii bcd2ascii_1 (
    .N({4'b0000, N}), .d3(bcd2ascii_1_d3), .d2(bcd2ascii_1_d2), .d1(bcd2ascii_1_d1), .d0(bcd2ascii_1_d0));  // open: d4
  vga_string vga_string_1 (
    .CX_i(CX_i), .CY_i(CY_i), .C_i(C_i), .fg_i(fg_i), .fg_c(fg_c), .CX_c(CX_c), .CY_c(CY_c),
    .C_0(bcd2ascii_1_d3), .C_1(bcd2ascii_1_d2), .C_2(bcd2ascii_1_d1), .C_3(bcd2ascii_1_d0), .en(en),
    .CX_o(CX_o), .CY_o(CY_o), .C_o(C_o), .fg_o(fg_o));
endmodule
