// Digital circuit vga_opdisp.dig as structural Verilog
module vga_opdisp (
  input  [15:0] fullop,
  input  [2:0] digit,
  output [6:0] char
);

  wire [6:0] op2ascii_1_l0, op2ascii_1_l1, op2ascii_1_l2, op2ascii_1_l3, op2ascii_1_l4, op2ascii_1_l5;

  op2ascii op2ascii_1 (
    .I(fullop[4:0]), .L0(op2ascii_1_l0), .L1(op2ascii_1_l1), .L2(op2ascii_1_l2), .L3(op2ascii_1_l3),
    .L4(op2ascii_1_l4), .L5(op2ascii_1_l5));
  Multiplexer #(.Selector_Bits(3), .Bits(7)) multiplexer_1 (
    .sel(digit), .in_0(7'b0100000), .in_1(7'b0100000), .in_2(op2ascii_1_l0), .in_3(op2ascii_1_l1),
    .in_4(op2ascii_1_l2), .in_5(op2ascii_1_l3), .in_6(op2ascii_1_l4), .in_7(op2ascii_1_l5), .out(char));
endmodule
