// Digital circuit vga_regdisp.dig as structural Verilog
module vga_regdisp (
  input  [15:0] \reg ,
  input  [2:0] digit,
  output [6:0] char
);

  wire [6:0] reg2ascii_1_d_0, reg2ascii_1_d_1, reg2ascii_1_d_2;

  reg2ascii reg2ascii_1 (
    .R(\reg [3:0]), .J(\reg [4]), .E(\reg [5]), .D_0(reg2ascii_1_d_0), .D_1(reg2ascii_1_d_1),
    .D_2(reg2ascii_1_d_2));
  Multiplexer #(.Selector_Bits(2), .Bits(7)) multiplexer_1 (
    .sel(digit[1:0]), .in_0(reg2ascii_1_d_0), .in_1(reg2ascii_1_d_1), .in_2(reg2ascii_1_d_2),
    .in_3(7'b0100000), .out(char));
endmodule
