// Digital circuit vga_text.dig as structural Verilog
module vga_text (
  input  H_i,
  input  V_i,
  input  pic,
  input  [4:0] row,
  input  [3:0] col,
  input  [15:0] CD,
  input  clock,
  input  [6:0] char,
  input  [11:0] fg,
  input  [11:0] bg,
  output [3:0] R,
  output [3:0] G,
  output [3:0] B,
  output hs,
  output vs,
  output de,
  output [10:0] CA
);

  wire d_ff_1_q, d_ff_2_q, d_ff_6_q, d_ff_9_q, d_ff_10_q;
  wire [1:0] d_ff_12_q;
  wire [3:0] d_ff_3_q, d_ff_11_q;
  wire [5:5] d_ff_5_q;
  wire [11:0] d_ff_7_q, d_ff_8_q, d_ff_13_q, d_ff_14_q, multiplexer_2_out;

  D_FF d_ff_1 (.D(H_i), .C(clock), .Q(d_ff_1_q));  // open: nQ
  D_FF d_ff_2 (.D(V_i), .C(clock), .Q(d_ff_2_q));  // open: nQ
  D_FF #(.Bits(4)) d_ff_3 (.D(col), .C(clock), .Q(d_ff_3_q));  // open: nQ
  D_FF #(.Bits(5)) d_ff_4 (.D(row), .C(clock), .Q(CA[4:0]));  // open: nQ
  D_FF #(.Bits(7)) d_ff_5 (.D(char), .C(clock), .Q({CA[10], d_ff_5_q[5], CA[9:5]}));  // open: nQ
  D_FF d_ff_6 (.D(pic), .C(clock), .Q(d_ff_6_q));  // open: nQ
  D_FF #(.Bits(12)) d_ff_7 (.D(bg), .C(clock), .Q(d_ff_7_q));  // open: nQ
  D_FF #(.Bits(12)) d_ff_8 (.D(fg), .C(clock), .Q(d_ff_8_q));  // open: nQ
  D_FF d_ff_9 (.D(d_ff_1_q), .C(clock), .Q(d_ff_9_q));  // open: nQ
  D_FF d_ff_10 (.D(d_ff_2_q), .C(clock), .Q(d_ff_10_q));  // open: nQ
  D_FF #(.Bits(4)) d_ff_11 (.D(d_ff_3_q), .C(clock), .Q(d_ff_11_q));  // open: nQ
  D_FF d_ff_12 (.D(d_ff_6_q), .C(clock), .Q(d_ff_12_q[1]));  // open: nQ
  D_FF #(.Bits(12)) d_ff_13 (.D(d_ff_7_q), .C(clock), .Q(d_ff_13_q));  // open: nQ
  D_FF #(.Bits(12)) d_ff_14 (.D(d_ff_8_q), .C(clock), .Q(d_ff_14_q));  // open: nQ
  Multiplexer #(.Selector_Bits(4)) multiplexer_1 (
    .sel(d_ff_11_q), .in_0(CD[15]), .in_1(CD[14]), .in_2(CD[13]), .in_3(CD[12]), .in_4(CD[11]),
    .in_5(CD[10]), .in_6(CD[9]), .in_7(CD[8]), .in_8(CD[7]), .in_9(CD[6]), .in_10(CD[5]), .in_11(CD[4]),
    .in_12(CD[3]), .in_13(CD[2]), .in_14(CD[1]), .in_15(CD[0]), .out(d_ff_12_q[0]));
  Multiplexer #(.Selector_Bits(2), .Bits(12)) multiplexer_2 (
    .sel(d_ff_12_q), .in_0({12{1'b0}}), .in_1({12{1'b0}}), .in_2(d_ff_13_q), .in_3(d_ff_14_q),
    .out(multiplexer_2_out));
  D_FF d_ff_15 (.D(d_ff_9_q), .C(clock), .Q(hs));  // open: nQ
  D_FF d_ff_16 (.D(d_ff_10_q), .C(clock), .Q(vs));  // open: nQ
  D_FF d_ff_17 (.D(d_ff_12_q[1]), .C(clock), .Q(de));  // open: nQ
  D_FF #(.Bits(4)) d_ff_18 (.D(multiplexer_2_out[3:0]), .C(clock), .Q(B));  // open: nQ
  D_FF #(.Bits(4)) d_ff_19 (.D(multiplexer_2_out[7:4]), .C(clock), .Q(G));  // open: nQ
  D_FF #(.Bits(4)) d_ff_20 (.D(multiplexer_2_out[11:8]), .C(clock), .Q(R));  // open: nQ

  // Other names for the same wires on the sheet: C = clock
endmodule
